// Logisim project 实验5-CS1805-U201814629-裴涵.circ as structural Verilog
module \四位二进制可逆计数器  (
  input  CPd,
  input  LD,
  input  A,
  input  B,
  input  C,
  input  CLR,
  input  CPu,
  input  D,
  output QA,
  output QB,
  output QC,
  output QD
);

  wire and_1_out, and_2_out, and_3_out, and_4_out, and_5_out, and_6_out, and_7_out, and_8_out, and_9_out,
       and_10_out, and_11_out, and_12_out, and_13_out, and_14_out, d_ff_1_qn, d_ff_2_qn, d_ff_3_qn,
       d_ff_4_qn, or_1_out, or_2_out, or_3_out, or_4_out, or_5_out, or_6_out, or_7_out, or_8_out;

  or or_1 (or_1_out, CPd, CPu);
  and and_1 (and_1_out, d_ff_1_qn, CPd);
  or or_2 (or_2_out, and_1_out, and_2_out);
  and and_2 (and_2_out, CPu, ~d_ff_1_qn);  // AND_Gate
  and and_3 (and_3_out, d_ff_2_qn, d_ff_1_qn, CPd);
  and and_4 (and_4_out, ~d_ff_2_qn, ~d_ff_1_qn, CPu);  // AND_Gate
  and and_5 (and_5_out, d_ff_3_qn, d_ff_2_qn, d_ff_1_qn, CPd);
  and and_6 (and_6_out, ~d_ff_3_qn, ~d_ff_2_qn, ~d_ff_1_qn, CPu);  // AND_Gate
  or or_3 (or_3_out, and_3_out, and_4_out);
  or or_4 (or_4_out, and_5_out, and_6_out);
  D_Flip_Flop #(.trigger("falling"), .Pre_Clr_Positions("LEGACY"), .NegatePresetClear("false"), .enable("true"), .NewFFLayout("false")) d_ff_1 (
    .clk(or_1_out), .D(d_ff_1_qn), .Q(QA), .Qn(d_ff_1_qn), .preset(and_13_out), .reset(or_7_out));  // open: en
  D_Flip_Flop #(.trigger("falling"), .Pre_Clr_Positions("LEGACY"), .NegatePresetClear("false"), .enable("true"), .NewFFLayout("false")) d_ff_2 (
    .clk(or_2_out), .D(d_ff_2_qn), .Q(QB), .Qn(d_ff_2_qn), .preset(and_7_out), .reset(or_5_out));  // open: en
  or or_5 (or_5_out, and_8_out, CLR);
  D_Flip_Flop #(.trigger("falling"), .Pre_Clr_Positions("LEGACY"), .NegatePresetClear("false"), .enable("true"), .NewFFLayout("false")) d_ff_3 (
    .clk(or_3_out), .D(d_ff_3_qn), .Q(QC), .Qn(d_ff_3_qn), .preset(and_10_out), .reset(or_6_out));  // open: en
  or or_6 (or_6_out, and_9_out, CLR);
  D_Flip_Flop #(.trigger("falling"), .Pre_Clr_Positions("LEGACY"), .NegatePresetClear("false"), .enable("true"), .NewFFLayout("false")) d_ff_4 (
    .clk(or_4_out), .D(d_ff_4_qn), .Q(QD), .Qn(d_ff_4_qn), .preset(and_14_out), .reset(or_8_out));  // open: en
  or or_7 (or_7_out, and_12_out, CLR);
  and and_7 (and_7_out, ~LD, ~CLR, B);  // AND_Gate
  and and_8 (and_8_out, ~B, ~LD);  // AND_Gate
  and and_9 (and_9_out, ~LD, ~C);  // AND_Gate
  and and_10 (and_10_out, ~CLR, ~LD, C);  // AND_Gate
  and and_11 (and_11_out, ~LD, ~D);  // AND_Gate
  or or_8 (or_8_out, CLR, and_11_out);
  and and_12 (and_12_out, ~LD, ~A);  // AND_Gate
  and and_13 (and_13_out, A, ~LD, ~CLR);  // AND_Gate
  and and_14 (and_14_out, ~CLR, ~LD, D);  // AND_Gate
endmodule

module \六十进制计数器  (
  input  in_1,
  input  in_2,
  input  in_3,
  input  in_4,
  output out_5,
  output out_6,
  output out_7,
  output out_8,
  output out_9,
  output out_10,
  output out_11,
  output out_12
);

  wire and_1_out, and_2_out, or_1_out, or_2_out;

  and and_1 (and_1_out, in_1, or_1_out);
  or or_1 (or_1_out, out_8, out_7, out_6, out_5);
  and and_2 (and_2_out, ~out_8, out_7, ~out_6, out_5);  // AND_Gate
  or or_2 (or_2_out, and_2_out, in_2);
  \四位二进制可逆计数器  \u_四位二进制可逆计数器_1  (
    .CPd(and_1_out), .CPu(in_3), .QA(out_8), .LD(1'b1), .A(1'b1), .QB(out_7), .B(1'b1), .QC(out_6), .C(1'b1),
    .CLR(or_2_out), .QD(out_5), .D(1'b1));
  \四位二进制可逆计数器  \u_四位二进制可逆计数器_2  (
    .CPd(in_4), .CPu(and_2_out), .QA(out_12), .LD(1'b1), .A(1'b1), .QB(out_11), .B(1'b1), .QC(out_10),
    .C(1'b1), .CLR(or_2_out), .QD(out_9), .D(1'b1));
endmodule
